# Fritzing sketch circuit (saved by Fritzing 0.9.3b)

parts:
  Part1 = Arduino Nano (Rev3.0) (ICSP)
  HC-SR04_Sensor_1 = HC-SR04 Ultrasonic Distance Sensor
  Part2 = Bluetooth HC-05 Macho
  U1 = Vibration Motor- ROB-08449 [package=vibe-motor-10mm]

nets:
  GND: Part1.GND, HC-SR04_Sensor_1.ECHO, Part2.GND, U1.-
  N1: Part1.D2, HC-SR04_Sensor_1.GND
  N2: Part1.D3, HC-SR04_Sensor_1.TRIG
  N3: Part1.D4, Part2.RXD
  N4: Part1.D5, Part2.TXD
  N5: Part1.D6, U1.+
  VCC: Part1.5V, HC-SR04_Sensor_1.VCC, Part2.VCC
